# Fritzing sketch circuit diagram (saved by Fritzing 0.9.3b)
breadboards: 1

parts:
  U2 = NodeMCU V1.0
  U3 = 74HC4051 [package=so16]
  U4 = GAS_SENSOR [package=mq-3]
  R2 = Photocell (LDR) [package=THT]
  R1 = Temperature Sensor (Thermistor) [thermistor_type=NTC package=THT]

nets:
  N1: U2.D2, U3.C
  N2: U2.D3, U3.B
  N3: U2.D4, U3.A
  3V3: U2.3V3, U3.VDD, U4.H2, R2.pin_0, R1.pin_0
  N4: U2.GND, U4.H1, R2.pin_1, R1.pin_1
  N5: U2.A0, U3.IO
  N6: U3.INH, U3.VSS
  N7: U3.IO2, U4.B1

custom parts:
  NodeMCU V1.0: ESP8266 based NodeMCU
